// Logisim project log.circ as structural Verilog: 26 circuits, main circuit main
module main (
  input  c,
  input  [1:0] cmd,
  input  in_3,
  input  in_4,
  input  in_5,
  input  in_6,
  output out_7,
  output out_8,
  output out_9,
  output out_10
);

  wire and_1_out, and_2_out, and_3_out, and_4_out, and_5_out, and_6_out, and_7_out, and_8_out, and_9_out,
       and_10_out, and_11_out, and_12_out, and_13_out, and_14_out, and_15_out, and_16_out, and_17_out,
       and_18_out, and_19_out, and_20_out, and_21_out, and_22_out, memory4_1_out_7, memory4_1_out_8,
       memory4_2_out_7, memory4_2_out_8, memory4_2_out_9, memory4_2_out_10, memory4_3_out_7, memory4_3_out_8,
       memory4_3_out_9, memory4_3_out_10, memory4_4_out_7, memory4_4_out_8, memory4_4_out_9,
       memory4_4_out_10, memory4_5_out_7, memory4_5_out_8, memory4_5_out_9, memory4_5_out_10, not_1_out,
       not_2_out, plus_2_bits_1_s0, plus_2_bits_1_s1, step_index_1_q0, step_index_1_q1, two_to_four_dec_1_e0,
       two_to_four_dec_1_e1, two_to_four_dec_1_e2, two_to_four_dec_1_e3, two_to_four_dec_2_e0,
       two_to_four_dec_2_e1, two_to_four_dec_2_e2, two_to_four_dec_2_e3, undriven;

  two_to_four_dec two_to_four_dec_1 (
    .n0(cmd[0]), .n1(cmd[1]), .e0(two_to_four_dec_1_e0), .e1(two_to_four_dec_1_e1),
    .e2(two_to_four_dec_1_e2), .e3(two_to_four_dec_1_e3));
  memory4 memory4_1 (
    .d0(plus_2_bits_1_s0), .d1(plus_2_bits_1_s1), .c(c), .out_7(memory4_1_out_7), .out_8(memory4_1_out_8));  // open: d2, d3, r_w, out_9, out_10
  not not_1 (not_1_out, c);
  not not_2 (not_2_out, c);
  step_index step_index_1 (
    .n0(two_to_four_dec_1_e2), .n1(two_to_four_dec_1_e3), .q0(step_index_1_q0), .q1(step_index_1_q1));  // open: q2, q3
  and and_1 (and_1_out, not_1_out, step_index_1_q0);
  and and_2 (and_2_out, not_2_out, step_index_1_q1);
  two_to_four_dec two_to_four_dec_2 (
    .n0(memory4_1_out_7), .n1(memory4_1_out_8), .e0(two_to_four_dec_2_e0), .e1(two_to_four_dec_2_e1),
    .e2(two_to_four_dec_2_e2), .e3(two_to_four_dec_2_e3));
  plus_2_bits plus_2_bits_1 (
    .n0(memory4_1_out_7), .n1(memory4_1_out_8), .m0(and_1_out), .m1(and_2_out), .s0(plus_2_bits_1_s0),
    .s1(plus_2_bits_1_s1));  // open: c
  buf and_3 (and_3_out, two_to_four_dec_2_e0);  // AND_Gate
  buf and_4 (and_4_out, two_to_four_dec_2_e1);  // AND_Gate
  buf and_5 (and_5_out, two_to_four_dec_2_e2);  // AND_Gate
  buf and_6 (and_6_out, two_to_four_dec_2_e3);  // AND_Gate
  memory4 memory4_2 (
    .d0(in_3), .d1(in_4), .d2(in_5), .d3(in_6), .c(c), .r_w(and_3_out), .out_7(memory4_2_out_7),
    .out_8(memory4_2_out_8), .out_9(memory4_2_out_9), .out_10(memory4_2_out_10));
  memory4 memory4_3 (
    .d0(in_3), .d1(in_4), .d2(in_5), .d3(in_6), .c(c), .r_w(and_4_out), .out_7(memory4_3_out_7),
    .out_8(memory4_3_out_8), .out_9(memory4_3_out_9), .out_10(memory4_3_out_10));
  memory4 memory4_4 (
    .d0(in_3), .d1(in_4), .d2(in_5), .d3(in_6), .c(undriven), .r_w(and_5_out), .out_7(memory4_4_out_7),
    .out_8(memory4_4_out_8), .out_9(memory4_4_out_9), .out_10(memory4_4_out_10));
  memory4 memory4_5 (
    .d0(in_3), .d1(in_4), .d2(in_5), .d3(in_6), .r_w(and_6_out), .out_7(memory4_5_out_7),
    .out_8(memory4_5_out_8), .out_9(memory4_5_out_9), .out_10(memory4_5_out_10));  // open: c
  and and_7 (and_7_out, two_to_four_dec_2_e0, memory4_2_out_7);
  and and_8 (and_8_out, two_to_four_dec_2_e0, memory4_2_out_8);
  and and_9 (and_9_out, two_to_four_dec_2_e0, memory4_2_out_9);
  and and_10 (and_10_out, two_to_four_dec_2_e0, memory4_2_out_10);
  and and_11 (and_11_out, memory4_3_out_7, two_to_four_dec_2_e1);
  and and_12 (and_12_out, memory4_3_out_8, two_to_four_dec_2_e1);
  and and_13 (and_13_out, memory4_3_out_9, two_to_four_dec_2_e1);
  and and_14 (and_14_out, memory4_3_out_10, two_to_four_dec_2_e1);
  and and_15 (and_15_out, two_to_four_dec_2_e2, memory4_4_out_7);
  and and_16 (and_16_out, two_to_four_dec_2_e2, memory4_4_out_8);
  and and_17 (and_17_out, two_to_four_dec_2_e2, memory4_4_out_9);
  and and_18 (and_18_out, two_to_four_dec_2_e2, memory4_4_out_10);
  and and_19 (and_19_out, two_to_four_dec_2_e3, memory4_5_out_7);
  and and_20 (and_20_out, two_to_four_dec_2_e3, memory4_5_out_8);
  and and_21 (and_21_out, two_to_four_dec_2_e3, memory4_5_out_9);
  and and_22 (and_22_out, memory4_5_out_10, two_to_four_dec_2_e3);
  or4 or4_1 (.in_1(and_7_out), .in_2(and_11_out), .in_3(and_15_out), .in_4(and_19_out), .out_5(out_7));
  or4 or4_2 (.in_1(and_8_out), .in_2(and_12_out), .in_3(and_16_out), .in_4(and_20_out), .out_5(out_8));
  or4 or4_3 (.in_1(and_13_out), .in_2(and_17_out), .in_3(and_9_out), .in_4(and_21_out), .out_5(out_9));
  or4 or4_4 (.in_1(and_10_out), .in_2(and_14_out), .in_3(and_18_out), .in_4(and_22_out), .out_5(out_10));
endmodule

module rs_sync (
  input  r,
  input  c,
  input  s,
  output q,
  output neg_q
);

  wire and_1_out, and_2_out;

  and and_1 (and_1_out, r, c);
  and and_2 (and_2_out, c, s);
  rs rs_1 (.r(and_1_out), .s(and_2_out), .q(q), .neg_q(neg_q));
endmodule

module rs (
  input  r,
  input  s,
  output q,
  output neg_q
);

  wire or_1_out, or_2_out;

  or or_1 (or_1_out, r, neg_q);
  or or_2 (or_2_out, q, s);
  not not_1 (q, or_1_out);
  not not_2 (neg_q, or_2_out);
endmodule

module d_trigger (
  input  d,
  input  c,
  output q,
  output neg_q
);

  wire not_1_out;

  not not_1 (not_1_out, d);
  rs_sync rs_sync_1 (.r(not_1_out), .c(c), .s(d), .q(q), .neg_q(neg_q));
endmodule

module three_to_eight_dec (
  input  [2:0] in_1,
  output e0,
  output e1,
  output e2,
  output e3,
  output out_6,
  output e4,
  output e5,
  output e6,
  output e7
);

  wire not_1_out, not_2_out, not_3_out, not_4_out, not_5_out, not_6_out, not_7_out, not_8_out, not_9_out,
       not_10_out, not_11_out, not_12_out, undriven, undriven_2, undriven_3;

  not not_1 (not_1_out, undriven);
  not not_2 (not_2_out, undriven_3);
  not not_3 (not_3_out, undriven_2);
  not not_4 (not_4_out, undriven_3);
  not not_5 (not_5_out, undriven_2);
  not not_6 (not_6_out, undriven);
  not not_7 (not_7_out, undriven_2);
  not not_8 (not_8_out, undriven_2);
  not not_9 (not_9_out, undriven);
  not not_10 (not_10_out, undriven_3);
  not not_11 (not_11_out, undriven_3);
  not not_12 (not_12_out, undriven);
  and3 and3_1 (.in_1(not_1_out), .in_2(not_2_out), .in_3(not_3_out), .out_4(e0));
  and3 and3_2 (.in_1(undriven), .in_2(not_4_out), .in_3(not_5_out), .out_4(e1));
  and3 and3_3 (.in_1(not_6_out), .in_2(undriven_3), .in_3(not_7_out), .out_4(e2));
  and3 and3_4 (.in_1(undriven), .in_2(undriven_3), .in_3(not_8_out), .out_4(e3));
  and3 and3_5 (.in_1(not_9_out), .in_2(not_10_out), .in_3(undriven_2), .out_4(e4));
  and3 and3_6 (.in_1(undriven), .in_2(not_11_out), .in_3(undriven_2), .out_4(e5));
  and3 and3_7 (.in_1(not_12_out), .in_2(undriven_3), .in_3(undriven_2), .out_4(e6));
  and3 and3_8 (.in_1(undriven), .in_2(undriven_3), .in_3(undriven_2), .out_4(e7));
endmodule

module two_to_four_dec (
  input  n0,
  input  n1,
  output e0,
  output e1,
  output e2,
  output e3
);

  wire not_1_out, not_2_out, not_3_out, not_4_out;

  not not_1 (not_1_out, n0);
  and and_1 (e0, not_1_out, not_2_out);
  not not_2 (not_2_out, n1);
  and and_2 (e1, n0, not_3_out);
  not not_3 (not_3_out, n1);
  not not_4 (not_4_out, n0);
  and and_3 (e2, not_4_out, n1);
  and and_4 (e3, n0, n1);
endmodule

module and3 (
  input  in_1,
  input  in_2,
  input  in_3,
  output out_4
);

  wire and_1_out;

  and and_1 (and_1_out, in_1, in_2);
  and and_2 (out_4, and_1_out, in_3);
endmodule

module mux8 (
  input  n0,
  input  n1,
  input  n2,
  input  d0,
  input  d1,
  input  d2,
  input  d3,
  input  d4,
  input  d5,
  input  d6,
  input  d7,
  output q
);

  wire and_1_out, and_2_out, and_3_out, and_4_out, and_5_out, and_6_out, and_7_out, and_8_out,
       three_to_eight_dec_1_p4, three_to_eight_dec_1_p5, three_to_eight_dec_1_p6, three_to_eight_dec_1_p7,
       three_to_eight_dec_1_p8, three_to_eight_dec_1_p9, three_to_eight_dec_1_p10, three_to_eight_dec_1_p11;

  // three_to_eight_dec three_to_eight_dec_1: pin names not known; wires that end beside it: n0, n1, n2, three_to_eight_dec_1_p4, three_to_eight_dec_1_p5, three_to_eight_dec_1_p6, three_to_eight_dec_1_p7, three_to_eight_dec_1_p8, three_to_eight_dec_1_p9, three_to_eight_dec_1_p10, three_to_eight_dec_1_p11, three_to_eight_dec_1_p11
  and and_1 (and_1_out, three_to_eight_dec_1_p4, d0);
  and and_2 (and_2_out, three_to_eight_dec_1_p5, d1);
  and and_3 (and_3_out, three_to_eight_dec_1_p6, d2);
  and and_4 (and_4_out, three_to_eight_dec_1_p7, d3);
  and and_5 (and_5_out, three_to_eight_dec_1_p8, d4);
  and and_6 (and_6_out, three_to_eight_dec_1_p9, d5);
  and and_7 (and_7_out, three_to_eight_dec_1_p10, d6);
  and and_8 (and_8_out, three_to_eight_dec_1_p11, d7);
  or8 or8_1 (
    .in_1(and_1_out), .in_2(and_2_out), .in_3(and_3_out), .in_4(and_4_out), .in_5(and_5_out),
    .in_6(and_6_out), .in_7(and_7_out), .in_8(and_8_out), .out_9(q));
endmodule

module or8 (
  input  in_1,
  input  in_2,
  input  in_3,
  input  in_4,
  input  in_5,
  input  in_6,
  input  in_7,
  input  in_8,
  output out_9
);

  wire or4_1_out_5, or4_2_out_5;

  or4 or4_1 (.in_1(in_1), .in_2(in_2), .in_3(in_3), .in_4(in_4), .out_5(or4_1_out_5));
  or4 or4_2 (.in_1(in_5), .in_2(in_6), .in_3(in_7), .in_4(in_8), .out_5(or4_2_out_5));
  or or_1 (out_9, or4_1_out_5, or4_2_out_5);
endmodule

module or4 (
  input  in_1,
  input  in_2,
  input  in_3,
  input  in_4,
  output out_5
);

  wire or_1_out, or_2_out;

  or or_1 (or_1_out, in_1, in_2);
  or or_2 (or_2_out, in_3, in_4);
  or or_3 (out_5, or_1_out, or_2_out);
endmodule

module demux8 (
  input  n0,
  input  n1,
  input  n2,
  input  d,
  output q0,
  output q1,
  output q2,
  output q3,
  output q4,
  output q5,
  output q6,
  output q7
);

  wire three_to_eight_dec_1_p4, three_to_eight_dec_1_p5, three_to_eight_dec_1_p6, three_to_eight_dec_1_p7,
       three_to_eight_dec_1_p8, three_to_eight_dec_1_p9, three_to_eight_dec_1_p10, three_to_eight_dec_1_p11;

  // three_to_eight_dec three_to_eight_dec_1: pin names not known; wires that end beside it: n0, n1, n2, three_to_eight_dec_1_p4, three_to_eight_dec_1_p5, three_to_eight_dec_1_p6, three_to_eight_dec_1_p7, three_to_eight_dec_1_p8, three_to_eight_dec_1_p9, three_to_eight_dec_1_p10, three_to_eight_dec_1_p11, three_to_eight_dec_1_p11
  and and_1 (q0, three_to_eight_dec_1_p4, d);
  and and_2 (q1, three_to_eight_dec_1_p5, d);
  and and_3 (q2, three_to_eight_dec_1_p6, d);
  and and_4 (q3, three_to_eight_dec_1_p7, d);
  and and_5 (q4, three_to_eight_dec_1_p8, d);
  and and_6 (q5, three_to_eight_dec_1_p9, d);
  and and_7 (q6, three_to_eight_dec_1_p10, d);
  and and_8 (q7, three_to_eight_dec_1_p11, d);
endmodule

module mem8 (
  input  n0,
  input  n1,
  input  n2,
  input  r_w,
  input  c,
  input  d,
  output q
);

  wire and_1_out, d_trigger_1_q, d_trigger_2_q, d_trigger_3_q, d_trigger_4_q, d_trigger_5_q, d_trigger_6_q,
       d_trigger_7_q, d_trigger_8_q, demux8_1_q0, demux8_1_q1, demux8_1_q2, demux8_1_q3, demux8_1_q4,
       demux8_1_q5, demux8_1_q6, demux8_1_q7;

  and and_1 (and_1_out, r_w, c);
  demux8 demux8_1 (
    .n0(n0), .n1(n1), .n2(n2), .d(and_1_out), .q0(demux8_1_q0), .q1(demux8_1_q1), .q2(demux8_1_q2),
    .q3(demux8_1_q3), .q4(demux8_1_q4), .q5(demux8_1_q5), .q6(demux8_1_q6), .q7(demux8_1_q7));
  d_trigger d_trigger_1 (.d(d), .c(demux8_1_q0), .q(d_trigger_1_q));  // open: neg_q
  d_trigger d_trigger_2 (.d(d), .c(demux8_1_q1), .q(d_trigger_2_q));  // open: neg_q
  d_trigger d_trigger_3 (.d(d), .c(demux8_1_q2), .q(d_trigger_3_q));  // open: neg_q
  d_trigger d_trigger_4 (.d(d), .c(demux8_1_q3), .q(d_trigger_4_q));  // open: neg_q
  d_trigger d_trigger_5 (.d(d), .c(demux8_1_q4), .q(d_trigger_5_q));  // open: neg_q
  d_trigger d_trigger_6 (.d(d), .c(demux8_1_q5), .q(d_trigger_6_q));  // open: neg_q
  d_trigger d_trigger_7 (.d(d), .c(demux8_1_q6), .q(d_trigger_7_q));  // open: neg_q
  d_trigger d_trigger_8 (.d(d), .c(demux8_1_q7), .q(d_trigger_8_q));  // open: neg_q
  mux8 mux8_1 (
    .n0(n0), .n1(n1), .n2(n2), .d0(d_trigger_1_q), .d1(d_trigger_2_q), .d2(d_trigger_3_q),
    .d3(d_trigger_4_q), .d4(d_trigger_5_q), .d5(d_trigger_6_q), .d6(d_trigger_7_q), .d7(d_trigger_8_q), .q(q));
endmodule

module demux4 (
  input  n0,
  input  n1,
  input  d,
  output q0,
  output q1,
  output q2,
  output q3
);

  wire two_to_four_dec_1_e0, two_to_four_dec_1_e1, two_to_four_dec_1_e2, two_to_four_dec_1_e3;

  two_to_four_dec two_to_four_dec_1 (
    .n0(n0), .n1(n1), .e0(two_to_four_dec_1_e0), .e1(two_to_four_dec_1_e1), .e2(two_to_four_dec_1_e2),
    .e3(two_to_four_dec_1_e3));
  and and_1 (q0, two_to_four_dec_1_e0, d);
  and and_2 (q1, two_to_four_dec_1_e1, d);
  and and_3 (q2, two_to_four_dec_1_e2, d);
  and and_4 (q3, two_to_four_dec_1_e3, d);
endmodule

module mux4 (
  input  n0,
  input  n1,
  input  d0,
  input  d1,
  input  d2,
  input  d3,
  output q
);

  wire and_1_out, and_2_out, and_3_out, and_4_out, two_to_four_dec_1_e0, two_to_four_dec_1_e1,
       two_to_four_dec_1_e2, two_to_four_dec_1_e3;

  two_to_four_dec two_to_four_dec_1 (
    .n0(n0), .n1(n1), .e0(two_to_four_dec_1_e0), .e1(two_to_four_dec_1_e1), .e2(two_to_four_dec_1_e2),
    .e3(two_to_four_dec_1_e3));
  and and_1 (and_1_out, two_to_four_dec_1_e0, d0);
  and and_2 (and_2_out, two_to_four_dec_1_e1, d1);
  and and_3 (and_3_out, two_to_four_dec_1_e2, d2);
  and and_4 (and_4_out, two_to_four_dec_1_e3, d3);
  or4 or4_1 (.in_1(and_1_out), .in_2(and_2_out), .in_3(and_3_out), .in_4(and_4_out), .out_5(q));
endmodule

module mem4 (
  input  n0,
  input  n1,
  input  r_w,
  input  c,
  input  d,
  output q
);

  wire mem4_with_4_exit_1_q0, mem4_with_4_exit_1_q1, mem4_with_4_exit_1_q2, mem4_with_4_exit_1_q3;

  mem4_with_4_exit mem4_with_4_exit_1 (
    .n0(n0), .n1(n1), .r_w(r_w), .c(c), .d(d), .q0(mem4_with_4_exit_1_q0), .q1(mem4_with_4_exit_1_q1),
    .q2(mem4_with_4_exit_1_q2), .q3(mem4_with_4_exit_1_q3));
  mux4 mux4_1 (
    .n0(n0), .n1(n1), .d0(mem4_with_4_exit_1_q0), .d1(mem4_with_4_exit_1_q1), .d2(mem4_with_4_exit_1_q2),
    .d3(mem4_with_4_exit_1_q3), .q(q));
endmodule

module plus2 (
  input  in_1,
  input  in_2,
  output s,
  output c
);

  xor xor_1 (s, in_1, in_2);
  and and_1 (c, in_1, in_2);
endmodule

module plus3 (
  input  in_1,
  input  in_2,
  input  in_3,
  output s,
  output c
);

  wire plus2_1_c, plus2_1_s, plus2_2_c;

  plus2 plus2_1 (.in_1(in_2), .in_2(in_3), .s(plus2_1_s), .c(plus2_1_c));
  plus2 plus2_2 (.in_1(in_1), .in_2(plus2_1_s), .s(s), .c(plus2_2_c));
  or or_1 (c, plus2_2_c, plus2_1_c);
endmodule

module plus_2_bits (
  input  n0,
  input  n1,
  input  m0,
  input  m1,
  output s0,
  output s1,
  output c
);

  wire plus2_1_c;

  plus2 plus2_1 (.in_1(n0), .in_2(m0), .s(s0), .c(plus2_1_c));
  plus3 plus3_1 (.in_1(plus2_1_c), .in_2(n1), .in_3(m1), .s(s1), .c(c));
endmodule

module plus_3_bits (
  input  n0,
  input  n1,
  input  n2,
  input  m0,
  input  m1,
  input  m2,
  output s0,
  output s1,
  output s2,
  output c
);

  wire plus_2_bits_1_c;

  plus_2_bits plus_2_bits_1 (.n0(n0), .n1(n1), .m0(m0), .m1(m1), .s0(s0), .s1(s1), .c(plus_2_bits_1_c));
  plus3 plus3_1 (.in_1(plus_2_bits_1_c), .in_2(n2), .in_3(m2), .s(s2), .c(c));
endmodule

module stack (
);

  mem4_with_4_exit mem4_with_4_exit_1 ();  // open: n0, n1, r_w, c, d, q0, q1, q2, q3
endmodule

module mem4_with_4_exit (
  input  n0,
  input  n1,
  input  r_w,
  input  c,
  input  d,
  output q0,
  output q1,
  output q2,
  output q3
);

  wire and_1_out, demux4_1_q0, demux4_1_q1, demux4_1_q2, demux4_1_q3;

  and and_1 (and_1_out, r_w, c);
  demux4 demux4_1 (
    .n0(n0), .n1(n1), .d(and_1_out), .q0(demux4_1_q0), .q1(demux4_1_q1), .q2(demux4_1_q2), .q3(demux4_1_q3));
  d_trigger d_trigger_1 (.d(d), .c(demux4_1_q0), .q(q0));  // open: neg_q
  d_trigger d_trigger_2 (.d(d), .c(demux4_1_q1), .q(q1));  // open: neg_q
  d_trigger d_trigger_3 (.d(d), .c(demux4_1_q2), .q(q2));  // open: neg_q
  d_trigger d_trigger_4 (.d(d), .c(demux4_1_q3), .q(q3));  // open: neg_q
endmodule

module memory4 (
  input  d0,
  input  d1,
  input  d2,
  input  d3,
  input  c,
  input  r_w,
  output out_7,
  output out_8,
  output out_9,
  output out_10
);

  wire and_1_out, d_trigger_1_q, d_trigger_2_q, d_trigger_3_q, d_trigger_4_q, not_1_out;

  and and_1 (and_1_out, c, r_w);
  not not_1 (not_1_out, c);
  d_trigger d_trigger_1 (.d(d0), .c(and_1_out), .q(d_trigger_1_q));  // open: neg_q
  d_trigger d_trigger_2 (.d(d1), .c(and_1_out), .q(d_trigger_2_q));  // open: neg_q
  d_trigger d_trigger_3 (.d(d2), .c(and_1_out), .q(d_trigger_3_q));  // open: neg_q
  d_trigger d_trigger_4 (.d(d3), .c(and_1_out), .q(d_trigger_4_q));  // open: neg_q
  d_trigger d_trigger_5 (.d(d_trigger_1_q), .c(not_1_out), .q(out_7));  // open: neg_q
  d_trigger d_trigger_6 (.d(d_trigger_2_q), .c(not_1_out), .q(out_8));  // open: neg_q
  d_trigger d_trigger_7 (.d(d_trigger_3_q), .c(not_1_out), .q(out_9));  // open: neg_q
  d_trigger d_trigger_8 (.d(d_trigger_4_q), .c(not_1_out), .q(out_10));  // open: neg_q
endmodule

module plus_4_bits (
  input  n0,
  input  n1,
  input  n2,
  input  n3,
  input  m0,
  input  m1,
  input  m2,
  input  m3,
  output s0,
  output s1,
  output s2,
  output s3,
  output c
);

  wire plus_3_bits_1_c;

  plus_3_bits plus_3_bits_1 (
    .n0(n0), .n1(n1), .n2(n2), .m0(m0), .m1(m1), .m2(m2), .s0(s0), .s1(s1), .s2(s2), .c(plus_3_bits_1_c));
  plus3 plus3_1 (.in_1(plus_3_bits_1_c), .in_2(n3), .in_3(m3), .s(s3), .c(c));
endmodule

module one_to_two_dec (
  input  n0,
  output e0,
  output e1
);

  not not_1 (e0, n0);

  assign e1 = n0;
endmodule

module step_index (
  input  n0,
  input  n1,
  output q0,
  output q1,
  output q2,
  output q3
);


  assign q0 = n0;
  assign q1 = n1;
  assign q2 = n1;
  assign q3 = n1;
endmodule

module jk_trigger_sync (
  input  k,
  input  c,
  input  j,
  output q,
  output neg_q
);

  wire and_1_out, and_2_out, not_1_out, rs_sync_1_neg_q, rs_sync_1_q;

  and and_1 (and_1_out, q, k);
  and and_2 (and_2_out, j, neg_q);
  rs_sync rs_sync_1 (.r(and_1_out), .c(c), .s(and_2_out), .q(rs_sync_1_q), .neg_q(rs_sync_1_neg_q));
  not not_1 (not_1_out, c);
  rs_sync rs_sync_2 (.r(rs_sync_1_neg_q), .c(not_1_out), .s(rs_sync_1_q), .q(q), .neg_q(neg_q));
endmodule
