// Logisim project log01.circ as structural Verilog: 19 circuits, main circuit main
module main (
  input  in_1,
  input  [1:0] in_2,
  input  in_3,
  input  [2:0] in_4,
  input  [3:0] in_5,
  output [3:0] out_6,
  output [3:0] out_7,
  output [3:0] out_8,
  output [3:0] out_9,
  output [3:0] out_10,
  output [3:0] out_11
);

  stack stack_1 (
    .reset(in_1), .cmd(in_2), .sync(in_3), .index(in_4), .data(in_5), .d0(out_6), .d1(out_7), .d2(out_8),
    .d3(out_9), .d4(out_10), .input_data(out_11));  // open: out_12
endmodule

module rs_trigger (
  input  r,
  input  s,
  output q,
  output neg_q
);

  wire or_1_out, or_2_out;

  or or_1 (or_1_out, r, neg_q);
  or or_2 (or_2_out, q, s);
  not not_1 (q, or_1_out);
  not not_2 (neg_q, or_2_out);
endmodule

module rs_sync_trigger (
  input  r,
  input  c,
  input  s,
  output q,
  output neg_q
);

  wire and_1_out, and_2_out;

  and and_1 (and_1_out, r, c);
  and and_2 (and_2_out, c, s);
  rs_trigger rs_trigger_1 (.r(and_1_out), .s(and_2_out), .q(q), .neg_q(neg_q));
endmodule

module d_trigger (
  input  d,
  input  c,
  output q,
  output neg_q,
  output ready
);

  wire not_1_out;

  not not_1 (not_1_out, d);
  rs_sync_trigger rs_sync_trigger_1 (.r(not_1_out), .c(c), .s(d), .q(q), .neg_q(neg_q));
  is_equal is_equal_1 (.in_1(d), .in_2(q), .out_3(ready));
endmodule

module d_4_bits_trigger (
  input  reset,
  input  sync,
  input  [3:0] d,
  output [3:0] q,
  output ready
);

  wire d0, d1, d2, d3, d_trigger_1_neg_q, d_trigger_2_neg_q, d_trigger_3_neg_q, d_trigger_4_neg_q, not_1_out,
       r0, r1, r2, r3, SYNC_t;
  wire [3:0] bit_extender_1_out;

  assign bit_extender_1_out = {{3{not_1_out}}, not_1_out};  // Bit_Extender bit_extender_1
  not not_1 (not_1_out, reset);
  assign {d3, d2, d1, d0} = bit_extender_1_out & d;  // AND_Gate and_1, 4 bits wide
  or or_1 (SYNC_t, reset, sync);
  d_trigger d_trigger_1 (.d(d0), .c(SYNC_t), .q(q[0]), .neg_q(d_trigger_1_neg_q), .ready(r0));
  d_trigger d_trigger_2 (.d(d1), .c(SYNC_t), .q(q[1]), .neg_q(d_trigger_2_neg_q), .ready(r1));
  d_trigger d_trigger_3 (.d(d2), .c(SYNC_t), .q(q[2]), .neg_q(d_trigger_3_neg_q), .ready(r2));
  d_trigger d_trigger_4 (.d(d3), .c(SYNC_t), .q(q[3]), .neg_q(d_trigger_4_neg_q), .ready(r3));
  and and_2 (ready, r0, r1, r2, r3);
  // also tied to GND on the sheet: {d_trigger_1_neg_q, d_trigger_2_neg_q, d_trigger_3_neg_q, d_trigger_4_neg_q}
endmodule

module is_equal (
  input  in_1,
  input  in_2,
  output out_3
);

  wire and_1_out, and_2_out, not_1_out, not_2_out;

  not not_1 (not_1_out, in_2);
  not not_2 (not_2_out, in_1);
  and and_1 (and_1_out, in_1, in_2);
  and and_2 (and_2_out, not_1_out, not_2_out);
  or or_1 (out_3, and_1_out, and_2_out);
endmodule

module dec_3_to_8 (
  input  [2:0] in_1,
  output [7:0] out_2
);

  wire not_1_out, not_2_out, not_3_out, not_4_out, not_5_out, not_6_out, not_7_out, not_8_out, not_9_out,
       not_10_out, not_11_out, not_12_out;

  not not_1 (not_1_out, in_1[0]);
  not not_2 (not_2_out, in_1[1]);
  and and_1 (out_2[0], not_1_out, not_2_out, not_3_out);
  not not_3 (not_3_out, in_1[2]);
  not not_4 (not_4_out, in_1[1]);
  and and_2 (out_2[1], in_1[0], not_4_out, not_5_out);
  not not_5 (not_5_out, in_1[2]);
  not not_6 (not_6_out, in_1[0]);
  and and_3 (out_2[2], not_6_out, in_1[1], not_7_out);
  not not_7 (not_7_out, in_1[2]);
  and and_4 (out_2[3], in_1[0], in_1[1], not_8_out);
  not not_8 (not_8_out, in_1[2]);
  not not_9 (not_9_out, in_1[0]);
  not not_10 (not_10_out, in_1[1]);
  and and_5 (out_2[4], not_9_out, not_10_out, in_1[2]);
  not not_11 (not_11_out, in_1[1]);
  and and_6 (out_2[5], in_1[0], not_11_out, in_1[2]);
  not not_12 (not_12_out, in_1[0]);
  and and_7 (out_2[6], not_12_out, in_1[1], in_1[2]);
  and and_8 (out_2[7], in_1[0], in_1[1], in_1[2]);
endmodule

module dec_2_to_4 (
  input  [1:0] in_1,
  output [3:0] out_2
);

  wire not_1_out, not_2_out, not_3_out, not_4_out;

  not not_1 (not_1_out, in_1[0]);
  not not_2 (not_2_out, in_1[1]);
  not not_3 (not_3_out, in_1[1]);
  not not_4 (not_4_out, in_1[0]);
  and and_1 (out_2[0], not_1_out, not_2_out);
  and and_2 (out_2[1], in_1[0], not_3_out);
  and and_3 (out_2[2], not_4_out, in_1[1]);
  and and_4 (out_2[3], in_1[0], in_1[1]);
endmodule

module d_3_bits_trigger (
  input  reset,
  input  sync,
  input  [2:0] d,
  output [2:0] q,
  output ready
);

  wire [3:3] d_4_bits_trigger_1_q;

  d_4_bits_trigger d_4_bits_trigger_1 (
    .reset(reset), .sync(sync), .d({1'b0, d}), .q({d_4_bits_trigger_1_q[3], q}), .ready(ready));
  // also tied to GND on the sheet: d_4_bits_trigger_1_q[3]
endmodule

module current_index (
  input  reset,
  input  [1:0] cmd,
  input  sync,
  output ready,
  output [2:0] index
);

  wire not_1_out;
  wire [2:0] and_3_out, bit_extender_1_out, d_3_bits_trigger_2_q, NEXT_IDX, xor_1_out;

  assign bit_extender_1_out = {{2{sync}}, sync};  // Bit_Extender bit_extender_1
  xor xor_1 (xor_1_out[0], cmd[0], cmd[1]);
  and and_1 (xor_1_out[1], xor_1_out[0], cmd[1]);
  and and_2 (xor_1_out[2], cmd[1], xor_1_out[0]);
  d_3_bits_trigger d_3_bits_trigger_1 (.reset(reset), .sync(sync), .d(NEXT_IDX), .q(index));  // open: ready
  not not_1 (not_1_out, sync);
  assign and_3_out = xor_1_out & bit_extender_1_out;  // AND_Gate and_3, 3 bits wide
  plus_3_bits_mod_5 plus_3_bits_mod_5_1 (.in_1(and_3_out), .in_2(d_3_bits_trigger_2_q), .out_3(NEXT_IDX));
  d_3_bits_trigger d_3_bits_trigger_2 (
    .reset(reset), .sync(not_1_out), .d(index), .q(d_3_bits_trigger_2_q), .ready(ready));
endmodule

module plus_3_bits (
  input  [2:0] in_1,
  input  [2:0] in_2,
  output [2:0] q,
  output c
);

  wire plus_2_bits_1_c;

  plus_2_bits plus_2_bits_1 (
    .n0(in_1[0]), .n1(in_1[1]), .m0(in_2[0]), .m1(in_2[1]), .s0(q[0]), .s1(q[1]), .c(plus_2_bits_1_c));
  plus3 plus3_1 (.in_1(plus_2_bits_1_c), .in_2(in_1[2]), .in_3(in_2[2]), .s(q[2]), .c(c));
endmodule

module plus2 (
  input  in_1,
  input  in_2,
  output s,
  output c
);

  xor xor_1 (s, in_1, in_2);
  and and_1 (c, in_1, in_2);
endmodule

module plus3 (
  input  in_1,
  input  in_2,
  input  in_3,
  output s,
  output c
);

  wire plus2_1_c, plus2_1_s, plus2_2_c;

  plus2 plus2_1 (.in_1(in_2), .in_2(in_3), .s(plus2_1_s), .c(plus2_1_c));
  plus2 plus2_2 (.in_1(in_1), .in_2(plus2_1_s), .s(s), .c(plus2_2_c));
  or or_1 (c, plus2_2_c, plus2_1_c);
endmodule

module plus_2_bits (
  input  n0,
  input  n1,
  input  m0,
  input  m1,
  output s0,
  output s1,
  output c
);

  wire plus2_1_c;

  plus2 plus2_1 (.in_1(n0), .in_2(m0), .s(s0), .c(plus2_1_c));
  plus3 plus3_1 (.in_1(plus2_1_c), .in_2(n1), .in_3(m1), .s(s1), .c(c));
endmodule

module plus_3_bits_mod_5 (
  input  [2:0] in_1,
  input  [2:0] in_2,
  output [2:0] out_3
);

  wire or_1_out, plus_3_bits_1_c, plus_3_bits_2_c;
  wire [1:1] and_1_out;
  wire [2:0] plus_3_bits_1_q;

  plus_3_bits plus_3_bits_1 (.in_1(in_1), .in_2(in_2), .q(plus_3_bits_1_q), .c(plus_3_bits_1_c));
  or or_1 (or_1_out, plus_3_bits_1_q[0], plus_3_bits_1_q[1]);
  and and_1 (and_1_out[1], or_1_out, plus_3_bits_1_q[2]);
  plus_3_bits plus_3_bits_2 (.in_1(plus_3_bits_1_q), .in_2({1'b0, {2{and_1_out[1]}}}), .q(out_3), .c(plus_3_bits_2_c));
  // also tied to GND on the sheet: {plus_3_bits_1_c, plus_3_bits_2_c}
endmodule

module memory (
  input  reset,
  input  sync,
  input  [1:0] cmd,
  input  [2:0] index,
  input  [3:0] data,
  output [3:0] q0,
  output [3:0] q1,
  output [3:0] q2,
  output [3:0] q3,
  output [3:0] q4,
  output [3:0] Q
);

  wire and_1_out, and_2_out, and_3_out, and_4_out, and_5_out, and_6_out, and_7_out, d_4_bits_trigger_1_ready,
       d_4_bits_trigger_2_ready, d_4_bits_trigger_3_ready, d_4_bits_trigger_4_ready,
       d_4_bits_trigger_5_ready, not_1_out;
  wire [3:0] and_8_out, and_9_out, and_10_out, and_11_out, and_12_out, bit_extender_1_out,
       bit_extender_2_out, bit_extender_3_out, bit_extender_4_out, bit_extender_5_out;
  wire [7:0] dec_3_to_8_1_out_2;

  not not_1 (not_1_out, cmd[1]);
  and and_1 (and_1_out, cmd[0], not_1_out);
  and and_2 (and_2_out, sync, and_1_out);
  dec_3_to_8 dec_3_to_8_1 (.in_1(index), .out_2(dec_3_to_8_1_out_2));
  and and_3 (and_3_out, and_2_out, dec_3_to_8_1_out_2[0]);
  and and_4 (and_4_out, and_2_out, dec_3_to_8_1_out_2[1]);
  and and_5 (and_5_out, and_2_out, dec_3_to_8_1_out_2[2]);
  and and_6 (and_6_out, and_2_out, dec_3_to_8_1_out_2[3]);
  and and_7 (and_7_out, and_2_out, dec_3_to_8_1_out_2[4]);
  assign bit_extender_1_out = {{3{dec_3_to_8_1_out_2[0]}}, dec_3_to_8_1_out_2[0]};  // Bit_Extender bit_extender_1
  assign bit_extender_2_out = {{3{dec_3_to_8_1_out_2[1]}}, dec_3_to_8_1_out_2[1]};  // Bit_Extender bit_extender_2
  assign bit_extender_3_out = {{3{dec_3_to_8_1_out_2[2]}}, dec_3_to_8_1_out_2[2]};  // Bit_Extender bit_extender_3
  assign bit_extender_4_out = {{3{dec_3_to_8_1_out_2[3]}}, dec_3_to_8_1_out_2[3]};  // Bit_Extender bit_extender_4
  assign bit_extender_5_out = {{3{dec_3_to_8_1_out_2[4]}}, dec_3_to_8_1_out_2[4]};  // Bit_Extender bit_extender_5
  assign and_8_out = bit_extender_1_out & q0;  // AND_Gate and_8, 4 bits wide
  assign and_9_out = bit_extender_2_out & q1;  // AND_Gate and_9, 4 bits wide
  assign and_10_out = bit_extender_3_out & q2;  // AND_Gate and_10, 4 bits wide
  assign and_11_out = bit_extender_4_out & q3;  // AND_Gate and_11, 4 bits wide
  assign and_12_out = bit_extender_5_out & q4;  // AND_Gate and_12, 4 bits wide
  assign Q = and_8_out | and_9_out | and_10_out | and_11_out | and_12_out;  // OR_Gate or_1, 4 bits wide
  d_4_bits_trigger d_4_bits_trigger_1 (
    .reset(reset), .sync(and_3_out), .d(data), .q(q0), .ready(d_4_bits_trigger_1_ready));
  d_4_bits_trigger d_4_bits_trigger_2 (
    .reset(reset), .sync(and_4_out), .d(data), .q(q1), .ready(d_4_bits_trigger_2_ready));
  d_4_bits_trigger d_4_bits_trigger_3 (
    .reset(reset), .sync(and_5_out), .d(data), .q(q2), .ready(d_4_bits_trigger_3_ready));
  d_4_bits_trigger d_4_bits_trigger_4 (
    .reset(reset), .sync(and_6_out), .d(data), .q(q3), .ready(d_4_bits_trigger_4_ready));
  d_4_bits_trigger d_4_bits_trigger_5 (
    .reset(reset), .sync(and_7_out), .d(data), .q(q4), .ready(d_4_bits_trigger_5_ready));
  // also tied to GND on the sheet: {dec_3_to_8_1_out_2[5], dec_3_to_8_1_out_2[6], dec_3_to_8_1_out_2[7], d_4_bits_trigger_1_ready, d_4_bits_trigger_2_ready, d_4_bits_trigger_3_ready, d_4_bits_trigger_4_ready, d_4_bits_trigger_5_ready}
endmodule

module stack (
  input  reset,
  input  [1:0] cmd,
  input  sync,
  input  [2:0] index,
  input  [3:0] data,
  output [3:0] d0,
  output [3:0] d1,
  output [3:0] d2,
  output [3:0] d3,
  output [3:0] d4,
  output [3:0] input_data,
  output [2:0] out_12
);

  wire and_1_out, current_index_1_ready, slow_1_out_2;
  wire [2:0] plus_3_bits_mod_5_1_out_3, shift_index_1_shift_idx;

  current_index current_index_1 (.reset(reset), .cmd(cmd), .sync(sync), .ready(current_index_1_ready), .index(out_12));
  shift_index shift_index_1 (.cmd(cmd), .index(index), .shift_idx(shift_index_1_shift_idx));
  and and_1 (and_1_out, sync, slow_1_out_2);
  slow slow_1 (.in_1(current_index_1_ready), .out_2(slow_1_out_2));
  plus_3_bits_mod_5 plus_3_bits_mod_5_1 (
    .in_1(out_12), .in_2(shift_index_1_shift_idx), .out_3(plus_3_bits_mod_5_1_out_3));
  memory memory_1 (
    .reset(reset), .sync(and_1_out), .cmd(cmd), .index(plus_3_bits_mod_5_1_out_3), .data(data), .q0(d0),
    .q1(d1), .q2(d2), .q3(d3), .q4(d4), .Q(input_data));
endmodule

module shift_index (
  input  [1:0] cmd,
  input  [2:0] index,
  output [2:0] shift_idx
);

  wire and_1_out, and_2_out;
  wire [2:0] and_3_out, and_4_out, bit_extender_1_out, bit_extender_2_out;

  and and_1 (and_1_out, ~cmd[0], cmd[1]);  // AND_Gate
  assign bit_extender_1_out = {{2{and_1_out}}, and_1_out};  // Bit_Extender bit_extender_1
  and and_2 (and_2_out, cmd[0], cmd[1]);
  assign and_3_out = 3'b001 & bit_extender_1_out;  // AND_Gate and_3, 3 bits wide
  assign bit_extender_2_out = {{2{and_2_out}}, and_2_out};  // Bit_Extender bit_extender_2
  assign and_4_out = bit_extender_2_out & index;  // AND_Gate and_4, 3 bits wide
  assign shift_idx = and_3_out | and_4_out;  // OR_Gate or_1, 3 bits wide
endmodule

module slow (
  input  in_1,
  output out_2
);

  wire not_1_out, not_2_out, not_3_out, not_4_out, not_5_out, not_6_out, not_7_out, not_8_out, not_9_out,
       not_10_out, not_11_out, not_12_out, not_13_out, not_14_out, not_15_out, not_16_out, not_17_out,
       not_18_out, not_19_out, not_20_out, not_21_out, not_22_out, not_23_out, not_24_out, not_25_out,
       not_26_out, not_27_out, not_28_out, not_29_out, not_30_out, not_31_out, not_32_out, not_33_out,
       not_34_out, not_35_out, not_36_out, not_37_out, not_38_out, not_39_out, not_40_out, not_41_out,
       not_42_out, not_43_out, not_44_out, not_45_out, not_46_out, not_47_out, not_48_out, not_49_out,
       not_50_out, not_51_out, not_52_out, not_53_out, not_54_out, not_55_out, not_56_out, not_57_out,
       not_58_out, not_59_out, not_60_out, not_61_out, not_62_out, not_63_out, not_64_out, not_65_out,
       not_66_out, not_67_out, not_68_out, not_69_out, not_70_out, not_71_out, not_72_out, not_73_out,
       not_74_out, not_75_out, not_76_out, not_77_out, not_78_out, not_79_out, not_80_out, not_81_out,
       not_82_out, not_83_out, not_84_out, not_85_out, not_86_out, not_87_out, not_88_out, not_89_out;

  not not_1 (not_1_out, in_1);
  not not_2 (not_2_out, not_1_out);
  not not_3 (not_3_out, not_85_out);
  not not_4 (not_4_out, not_3_out);
  not not_5 (not_5_out, not_86_out);
  not not_6 (not_6_out, not_5_out);
  not not_7 (not_7_out, not_87_out);
  not not_8 (not_8_out, not_7_out);
  not not_9 (not_9_out, not_88_out);
  not not_10 (not_10_out, not_9_out);
  not not_11 (not_11_out, not_89_out);
  not not_12 (not_12_out, not_11_out);
  not not_13 (not_13_out, not_2_out);
  not not_14 (not_14_out, not_13_out);
  not not_15 (not_15_out, not_4_out);
  not not_16 (not_16_out, not_15_out);
  not not_17 (not_17_out, not_6_out);
  not not_18 (not_18_out, not_17_out);
  not not_19 (not_19_out, not_8_out);
  not not_20 (not_20_out, not_19_out);
  not not_21 (not_21_out, not_10_out);
  not not_22 (not_22_out, not_21_out);
  not not_23 (not_23_out, not_12_out);
  not not_24 (not_24_out, not_23_out);
  not not_25 (not_25_out, not_14_out);
  not not_26 (not_26_out, not_25_out);
  not not_27 (not_27_out, not_16_out);
  not not_28 (not_28_out, not_27_out);
  not not_29 (not_29_out, not_18_out);
  not not_30 (not_30_out, not_29_out);
  not not_31 (not_31_out, not_20_out);
  not not_32 (not_32_out, not_31_out);
  not not_33 (not_33_out, not_22_out);
  not not_34 (not_34_out, not_33_out);
  not not_35 (not_35_out, not_24_out);
  not not_36 (not_36_out, not_35_out);
  not not_37 (not_37_out, not_26_out);
  not not_38 (not_38_out, not_37_out);
  not not_39 (not_39_out, not_28_out);
  not not_40 (not_40_out, not_39_out);
  not not_41 (not_41_out, not_30_out);
  not not_42 (not_42_out, not_41_out);
  not not_43 (not_43_out, not_32_out);
  not not_44 (not_44_out, not_43_out);
  not not_45 (not_45_out, not_34_out);
  not not_46 (not_46_out, not_45_out);
  not not_47 (not_47_out, not_36_out);
  not not_48 (not_48_out, not_47_out);
  not not_49 (not_49_out, not_38_out);
  not not_50 (not_50_out, not_49_out);
  not not_51 (not_51_out, not_40_out);
  not not_52 (not_52_out, not_51_out);
  not not_53 (not_53_out, not_42_out);
  not not_54 (not_54_out, not_53_out);
  not not_55 (not_55_out, not_44_out);
  not not_56 (not_56_out, not_55_out);
  not not_57 (not_57_out, not_46_out);
  not not_58 (not_58_out, not_57_out);
  not not_59 (not_59_out, not_48_out);
  not not_60 (not_60_out, not_59_out);
  not not_61 (not_61_out, not_50_out);
  not not_62 (not_62_out, not_61_out);
  not not_63 (not_63_out, not_52_out);
  not not_64 (not_64_out, not_63_out);
  not not_65 (not_65_out, not_54_out);
  not not_66 (not_66_out, not_65_out);
  not not_67 (not_67_out, not_56_out);
  not not_68 (not_68_out, not_67_out);
  not not_69 (not_69_out, not_58_out);
  not not_70 (not_70_out, not_69_out);
  not not_71 (not_71_out, not_60_out);
  not not_72 (not_72_out, not_71_out);
  not not_73 (not_73_out, not_62_out);
  not not_74 (not_74_out, not_73_out);
  not not_75 (not_75_out, not_64_out);
  not not_76 (not_76_out, not_75_out);
  not not_77 (not_77_out, not_66_out);
  not not_78 (not_78_out, not_77_out);
  not not_79 (not_79_out, not_68_out);
  not not_80 (not_80_out, not_79_out);
  not not_81 (not_81_out, not_70_out);
  not not_82 (not_82_out, not_81_out);
  not not_83 (not_83_out, not_72_out);
  not not_84 (not_84_out, not_83_out);
  not not_85 (not_85_out, not_74_out);
  not not_86 (not_86_out, not_76_out);
  not not_87 (not_87_out, not_78_out);
  not not_88 (not_88_out, not_80_out);
  not not_89 (not_89_out, not_82_out);
  not not_90 (out_2, not_84_out);
endmodule
