// Logisim project logisim_stack.circ as structural Verilog: 29 circuits, main circuit main
module main (
  input  reset,
  input  [1:0] COMMAND,
  input  sync,
  input  [2:0] index,
  input  [3:0] IO_DATA_in,
  output [3:0] out_6,
  output [3:0] out_7,
  output [3:0] out_8,
  output [3:0] out_9,
  output [3:0] out_10,
  output [3:0] IO_DATA_out
);

  stack stack_1 (
    .reset(reset), .cmd(COMMAND), .sync(sync), .index(index), .IO_DATA_in(IO_DATA_in), .out_6(out_6),
    .out_7(out_7), .out_8(out_8), .out_9(out_9), .out_10(out_10), .IO_DATA_out(IO_DATA_out));
endmodule

module rs_trigger (
  input  r,
  input  s,
  output q,
  output neg_q
);

  nor nor_1 (q, r, neg_q);
  nor nor_2 (neg_q, q, s);
endmodule

module rs_sync_trigger (
  input  r,
  input  c,
  input  s,
  output q,
  output neg_q
);

  wire and_1_out, and_2_out;

  and and_1 (and_1_out, r, c);
  and and_2 (and_2_out, c, s);
  rs_trigger rs_trigger_1 (.r(and_1_out), .s(and_2_out), .q(q), .neg_q(neg_q));
endmodule

module d_trigger (
  input  d,
  input  c,
  output q,
  output neg_q
);

  wire not_1_out;

  not not_1 (not_1_out, d);
  rs_sync_trigger rs_sync_trigger_1 (.r(not_1_out), .c(c), .s(d), .q(q), .neg_q(neg_q));
endmodule

module d_4_bits_trigger (
  input  reset,
  input  sync,
  input  [3:0] d,
  output [3:0] q
);

  wire d0, d1, d2, d3, d_trigger_1_neg_q, d_trigger_2_neg_q, d_trigger_3_neg_q, d_trigger_4_neg_q, not_1_out,
       SYNC_t;
  wire [3:0] bit_extender_1_out;

  assign bit_extender_1_out = {{3{not_1_out}}, not_1_out};  // Bit_Extender bit_extender_1
  not not_1 (not_1_out, reset);
  assign {d3, d2, d1, d0} = bit_extender_1_out & d;  // AND_Gate and_1, 4 bits wide
  or or_1 (SYNC_t, reset, sync);
  d_trigger d_trigger_1 (.d(d0), .c(SYNC_t), .q(q[0]), .neg_q(d_trigger_1_neg_q));
  d_trigger d_trigger_2 (.d(d1), .c(SYNC_t), .q(q[1]), .neg_q(d_trigger_2_neg_q));
  d_trigger d_trigger_3 (.d(d2), .c(SYNC_t), .q(q[2]), .neg_q(d_trigger_3_neg_q));
  d_trigger d_trigger_4 (.d(d3), .c(SYNC_t), .q(q[3]), .neg_q(d_trigger_4_neg_q));
endmodule

module is_equal (
  input  in_1,
  input  in_2,
  output out_3
);

  wire and_1_out, and_2_out, not_1_out, not_2_out;

  not not_1 (not_1_out, in_2);
  not not_2 (not_2_out, in_1);
  and and_1 (and_1_out, in_1, in_2);
  and and_2 (and_2_out, not_1_out, not_2_out);
  or or_1 (out_3, and_1_out, and_2_out);
endmodule

module dec_3_to_8 (
  input  [2:0] in_1,
  output [7:0] out_2
);

  wire not_1_out, not_2_out, not_3_out, not_4_out, not_5_out, not_6_out, not_7_out, not_8_out, not_9_out,
       not_10_out, not_11_out, not_12_out;

  not not_1 (not_1_out, in_1[0]);
  not not_2 (not_2_out, in_1[1]);
  and and_1 (out_2[0], not_1_out, not_2_out, not_3_out);
  not not_3 (not_3_out, in_1[2]);
  not not_4 (not_4_out, in_1[1]);
  and and_2 (out_2[1], in_1[0], not_4_out, not_5_out);
  not not_5 (not_5_out, in_1[2]);
  not not_6 (not_6_out, in_1[0]);
  and and_3 (out_2[2], not_6_out, in_1[1], not_7_out);
  not not_7 (not_7_out, in_1[2]);
  and and_4 (out_2[3], in_1[0], in_1[1], not_8_out);
  not not_8 (not_8_out, in_1[2]);
  not not_9 (not_9_out, in_1[0]);
  not not_10 (not_10_out, in_1[1]);
  and and_5 (out_2[4], not_9_out, not_10_out, in_1[2]);
  not not_11 (not_11_out, in_1[1]);
  and and_6 (out_2[5], in_1[0], not_11_out, in_1[2]);
  not not_12 (not_12_out, in_1[0]);
  and and_7 (out_2[6], not_12_out, in_1[1], in_1[2]);
  and and_8 (out_2[7], in_1[0], in_1[1], in_1[2]);
endmodule

module dec_2_to_4 (
  input  [1:0] in_1,
  output [3:0] out_2
);

  wire not_1_out, not_2_out, not_3_out, not_4_out;

  not not_1 (not_1_out, in_1[0]);
  not not_2 (not_2_out, in_1[1]);
  not not_3 (not_3_out, in_1[1]);
  not not_4 (not_4_out, in_1[0]);
  and and_1 (out_2[0], not_1_out, not_2_out);
  and and_2 (out_2[1], in_1[0], not_3_out);
  and and_3 (out_2[2], not_4_out, in_1[1]);
  and and_4 (out_2[3], in_1[0], in_1[1]);
endmodule

module d_3_bits_trigger (
  input  reset,
  input  sync,
  input  [2:0] d,
  output [2:0] q
);

  wire [3:3] d_4_bits_trigger_1_q;

  d_4_bits_trigger d_4_bits_trigger_1 (.reset(reset), .sync(sync), .d({1'b0, d}), .q({d_4_bits_trigger_1_q[3], q}));
  // also tied to GND on the sheet: d_4_bits_trigger_1_q[3]
endmodule

module current_index (
  input  reset,
  input  [1:0] cmd,
  input  sync,
  output [2:0] index
);

  wire not_1_out;
  wire [2:0] d_3_bits_trigger_1_q, d_3_bits_trigger_2_q;

  next_index next_index_1 (.cmd(cmd), .sync(sync), .index(d_3_bits_trigger_2_q), .next_idx(index));
  d_3_bits_trigger d_3_bits_trigger_1 (.reset(reset), .sync(sync), .d(index), .q(d_3_bits_trigger_1_q));
  not not_1 (not_1_out, sync);
  d_3_bits_trigger d_3_bits_trigger_2 (
    .reset(reset), .sync(not_1_out), .d(d_3_bits_trigger_1_q), .q(d_3_bits_trigger_2_q));

  // Other names for the same wires on the sheet: NEXT_IDX[2:0] = index
endmodule

module plus_3_bits (
  input  [2:0] in_1,
  input  [2:0] in_2,
  output [2:0] q,
  output c
);

  wire plus_2_bits_1_c;

  plus_2_bits plus_2_bits_1 (
    .n0(in_1[0]), .n1(in_1[1]), .m0(in_2[0]), .m1(in_2[1]), .s0(q[0]), .s1(q[1]), .c(plus_2_bits_1_c));
  plus3 plus3_1 (.in_1(plus_2_bits_1_c), .in_2(in_1[2]), .in_3(in_2[2]), .s(q[2]), .c(c));
endmodule

module plus2 (
  input  in_1,
  input  in_2,
  output s,
  output c
);

  xor xor_1 (s, in_1, in_2);
  and and_1 (c, in_1, in_2);
endmodule

module plus3 (
  input  in_1,
  input  in_2,
  input  in_3,
  output s,
  output c
);

  wire plus2_1_c, plus2_1_s, plus2_2_c;

  plus2 plus2_1 (.in_1(in_2), .in_2(in_3), .s(plus2_1_s), .c(plus2_1_c));
  plus2 plus2_2 (.in_1(in_1), .in_2(plus2_1_s), .s(s), .c(plus2_2_c));
  or or_1 (c, plus2_2_c, plus2_1_c);
endmodule

module plus_2_bits (
  input  n0,
  input  n1,
  input  m0,
  input  m1,
  output s0,
  output s1,
  output c
);

  wire plus2_1_c;

  plus2 plus2_1 (.in_1(n0), .in_2(m0), .s(s0), .c(plus2_1_c));
  plus3 plus3_1 (.in_1(plus2_1_c), .in_2(n1), .in_3(m1), .s(s1), .c(c));
endmodule

module plus_3_bits_mod_5 (
  input  [2:0] in_1,
  input  [2:0] in_2,
  output [2:0] out_3
);

  wire [2:0] plus_3_bits_1_q;
  wire [3:3] plus_3_bits_1_c;

  plus_3_bits plus_3_bits_1 (.in_1(in_1), .in_2(in_2), .q(plus_3_bits_1_q), .c(plus_3_bits_1_c[3]));
  bits_mod_5 bits_mod_5_1 (.in_1({plus_3_bits_1_c[3], plus_3_bits_1_q}), .out_2(out_3));
endmodule

module memory (
  input  reset,
  input  sync,
  input  [1:0] cmd,
  input  [2:0] index,
  input  [3:0] data,
  output [3:0] q0,
  output [3:0] q1,
  output [3:0] q2,
  output [3:0] q3,
  output [3:0] q4,
  output [3:0] Q
);

  wire and_1_out, and_2_out, and_3_out, and_4_out, and_5_out, and_6_out, and_7_out, not_1_out;
  wire [3:0] and_8_out, and_9_out, and_10_out, and_11_out, and_12_out, bit_extender_1_out,
       bit_extender_2_out, bit_extender_3_out, bit_extender_4_out, bit_extender_5_out;
  wire [7:0] dec_3_to_8_1_out_2;

  not not_1 (not_1_out, cmd[1]);
  and and_1 (and_1_out, cmd[0], not_1_out);
  and and_2 (and_2_out, sync, and_1_out);
  dec_3_to_8 dec_3_to_8_1 (.in_1(index), .out_2(dec_3_to_8_1_out_2));
  and and_3 (and_3_out, and_2_out, dec_3_to_8_1_out_2[0]);
  and and_4 (and_4_out, and_2_out, dec_3_to_8_1_out_2[1]);
  and and_5 (and_5_out, and_2_out, dec_3_to_8_1_out_2[2]);
  and and_6 (and_6_out, and_2_out, dec_3_to_8_1_out_2[3]);
  and and_7 (and_7_out, and_2_out, dec_3_to_8_1_out_2[4]);
  assign bit_extender_1_out = {{3{dec_3_to_8_1_out_2[0]}}, dec_3_to_8_1_out_2[0]};  // Bit_Extender bit_extender_1
  assign bit_extender_2_out = {{3{dec_3_to_8_1_out_2[1]}}, dec_3_to_8_1_out_2[1]};  // Bit_Extender bit_extender_2
  assign bit_extender_3_out = {{3{dec_3_to_8_1_out_2[2]}}, dec_3_to_8_1_out_2[2]};  // Bit_Extender bit_extender_3
  assign bit_extender_4_out = {{3{dec_3_to_8_1_out_2[3]}}, dec_3_to_8_1_out_2[3]};  // Bit_Extender bit_extender_4
  assign bit_extender_5_out = {{3{dec_3_to_8_1_out_2[4]}}, dec_3_to_8_1_out_2[4]};  // Bit_Extender bit_extender_5
  assign and_8_out = bit_extender_1_out & q0;  // AND_Gate and_8, 4 bits wide
  assign and_9_out = bit_extender_2_out & q1;  // AND_Gate and_9, 4 bits wide
  assign and_10_out = bit_extender_3_out & q2;  // AND_Gate and_10, 4 bits wide
  assign and_11_out = bit_extender_4_out & q3;  // AND_Gate and_11, 4 bits wide
  assign and_12_out = bit_extender_5_out & q4;  // AND_Gate and_12, 4 bits wide
  assign Q = and_8_out | and_9_out | and_10_out | and_11_out | and_12_out;  // OR_Gate or_1, 4 bits wide
  d_4_bits_trigger d_4_bits_trigger_1 (.reset(reset), .sync(and_3_out), .d(data), .q(q0));
  d_4_bits_trigger d_4_bits_trigger_2 (.reset(reset), .sync(and_4_out), .d(data), .q(q1));
  d_4_bits_trigger d_4_bits_trigger_3 (.reset(reset), .sync(and_5_out), .d(data), .q(q2));
  d_4_bits_trigger d_4_bits_trigger_4 (.reset(reset), .sync(and_6_out), .d(data), .q(q3));
  d_4_bits_trigger d_4_bits_trigger_5 (.reset(reset), .sync(and_7_out), .d(data), .q(q4));
  // also tied to GND on the sheet: {dec_3_to_8_1_out_2[5], dec_3_to_8_1_out_2[6], dec_3_to_8_1_out_2[7]}
endmodule

module stack (
  input  reset,
  input  [1:0] cmd,
  input  sync,
  input  [2:0] index,
  input  [3:0] IO_DATA_in,
  output [3:0] out_6,
  output [3:0] out_7,
  output [3:0] out_8,
  output [3:0] out_9,
  output [3:0] out_10,
  output [3:0] IO_DATA_out
);

  wire slow_1_out_2;
  wire [2:0] current_index_1_index, d_3_bits_trigger_1_q, shift_index_1_out_5;
  wire [3:0] memory_1_q;

  current_index current_index_1 (.reset(reset), .cmd(cmd), .sync(sync), .index(current_index_1_index));
  inout_cmd inout_cmd_1 (.cmd(cmd), .program_out(memory_1_q), .inpout(IO_DATA_in));
  shift_index shift_index_1 (
    .cmd(cmd), .sync(sync), .curr_idx(current_index_1_index), .index(index), .out_5(shift_index_1_out_5));
  slow slow_1 (.in_1(sync), .out_2(slow_1_out_2));
  d_3_bits_trigger d_3_bits_trigger_1 (.reset(reset), .sync(sync), .d(shift_index_1_out_5), .q(d_3_bits_trigger_1_q));
  memory memory_1 (
    .reset(reset), .sync(slow_1_out_2), .cmd(cmd), .index(d_3_bits_trigger_1_q), .data(IO_DATA_in),
    .q0(out_10), .q1(out_6), .q2(out_7), .q3(out_8), .q4(out_9), .Q(memory_1_q));

  assign IO_DATA_out = IO_DATA_in;

  // Other names for the same wires on the sheet: D0[3:0] = out_6; D1[3:0] = out_7; D2[3:0] = out_8; D3[3:0] = out_9;
  //   D4[3:0] = out_10; DATA[3:0] = IO_DATA_in
endmodule

module shift_index (
  input  [1:0] cmd,
  input  sync,
  input  [2:0] curr_idx,
  input  [2:0] index,
  output [2:0] out_5
);

  wire and_1_out, xor_1_out;
  wire [0:0] and_2_out;
  wire [2:0] and_3_out, bit_extender_1_out, next_index_1_next_idx;

  assign bit_extender_1_out = {{2{and_1_out}}, and_1_out};  // Bit_Extender bit_extender_1
  and and_1 (and_1_out, cmd[0], sync, cmd[1]);
  xor xor_1 (xor_1_out, cmd[0], cmd[1]);
  and and_2 (and_2_out[0], cmd[1], xor_1_out);
  next_index next_index_1 (.cmd({1'b0, and_2_out[0]}), .sync(sync), .index(curr_idx), .next_idx(next_index_1_next_idx));
  assign and_3_out = bit_extender_1_out & index;  // AND_Gate and_3, 3 bits wide
  plus_3_bits_mod_5 plus_3_bits_mod_5_1 (.in_1(next_index_1_next_idx), .in_2(and_3_out), .out_3(out_5));
endmodule

module slow (
  input  in_1,
  output out_2
);

  wire not_1_out, not_2_out, not_3_out, not_4_out, not_5_out, not_6_out, not_7_out, not_8_out, not_9_out,
       not_10_out, not_11_out, not_12_out, not_13_out, not_14_out, not_15_out, not_16_out, not_17_out,
       not_18_out, not_19_out, not_20_out, not_21_out, not_22_out, not_23_out, not_24_out, not_25_out,
       not_26_out, not_27_out, not_28_out, not_29_out, not_30_out, not_31_out, not_32_out, not_33_out,
       not_34_out, not_35_out, not_36_out, not_37_out, not_38_out, not_39_out, not_40_out, not_41_out,
       not_42_out, not_43_out, not_44_out, not_45_out, not_46_out, not_47_out, not_48_out, not_49_out,
       not_50_out, not_51_out, not_52_out, not_53_out, not_54_out, not_55_out, not_56_out, not_57_out,
       not_58_out, not_59_out, not_60_out, not_61_out, not_62_out, not_63_out, not_64_out, not_65_out,
       not_66_out, not_67_out, not_68_out, not_69_out, not_70_out, not_71_out, not_72_out, not_73_out,
       not_74_out, not_75_out, not_76_out, not_77_out, not_78_out, not_79_out, not_80_out, not_81_out,
       not_82_out, not_83_out, not_84_out, not_85_out, not_86_out, not_87_out, not_88_out, not_89_out,
       not_90_out, not_91_out, not_92_out, not_93_out, not_94_out, not_95_out, not_96_out, not_97_out,
       not_98_out, not_99_out, not_100_out, not_101_out, not_102_out, not_103_out, not_104_out, not_105_out,
       not_106_out, not_107_out, not_108_out, not_109_out, not_110_out, not_111_out, not_112_out,
       not_113_out, not_114_out, not_115_out, not_116_out, not_117_out, not_118_out, not_119_out,
       not_120_out, not_121_out, not_122_out, not_123_out, not_124_out, not_125_out, not_126_out,
       not_127_out, not_128_out, not_129_out, not_130_out, not_131_out, not_132_out, not_133_out,
       not_134_out, not_135_out, not_136_out, not_137_out, not_138_out, not_139_out, not_140_out,
       not_141_out, not_142_out, not_143_out, not_144_out, not_145_out, not_146_out, not_147_out,
       not_148_out, not_149_out, not_150_out, not_151_out, not_152_out, not_153_out, not_154_out,
       not_155_out, not_156_out, not_157_out, not_158_out, not_159_out, not_160_out, not_161_out,
       not_162_out, not_163_out, not_164_out, not_165_out, not_166_out, not_167_out, not_168_out,
       not_169_out, not_170_out, not_171_out, not_172_out, not_173_out, not_174_out, not_175_out,
       not_176_out, not_177_out, not_178_out, not_179_out, not_180_out, not_181_out, not_182_out,
       not_183_out, not_184_out, not_185_out, not_186_out, not_187_out, not_188_out, not_189_out,
       not_190_out, not_191_out, not_192_out, not_193_out, not_194_out, not_195_out, not_196_out,
       not_197_out, not_198_out, not_199_out, not_200_out, not_201_out, not_202_out, not_203_out,
       not_204_out, not_205_out, not_206_out, not_207_out, not_208_out, not_209_out, not_210_out,
       not_211_out, not_212_out, not_213_out, not_214_out, not_215_out, not_216_out, not_217_out,
       not_218_out, not_219_out, not_220_out, not_221_out, not_222_out, not_223_out, not_224_out,
       not_225_out, not_226_out, not_227_out, not_228_out, not_229_out, not_230_out, not_231_out,
       not_232_out, not_233_out, not_234_out, not_235_out, not_236_out, not_237_out, not_238_out,
       not_239_out, not_240_out, not_241_out, not_242_out, not_243_out, not_244_out, not_245_out,
       not_246_out, not_247_out, not_248_out, not_249_out, not_250_out, not_251_out, not_252_out,
       not_253_out, not_254_out, not_255_out, not_256_out, not_257_out, not_258_out, not_259_out,
       not_260_out, not_261_out, not_262_out, not_263_out, not_264_out, not_265_out, not_266_out,
       not_267_out, not_268_out, not_269_out, not_270_out, not_271_out, not_272_out, not_273_out,
       not_274_out, not_275_out, not_276_out, not_277_out, not_278_out, not_279_out, not_280_out,
       not_281_out, not_282_out, not_283_out, not_284_out, not_285_out, not_286_out, not_287_out,
       not_288_out, not_289_out, not_290_out, not_291_out, not_292_out, not_293_out, not_294_out,
       not_295_out, not_296_out, not_297_out, not_298_out, not_299_out, not_300_out, not_301_out,
       not_302_out, not_303_out, not_304_out, not_305_out, not_306_out, not_307_out, not_308_out,
       not_309_out, not_310_out, not_311_out, not_312_out, not_313_out, not_314_out, not_315_out,
       not_316_out, not_317_out, not_318_out, not_319_out, not_320_out, not_321_out, not_322_out,
       not_323_out, not_324_out, not_325_out, not_326_out, not_327_out, not_328_out, not_329_out,
       not_330_out, not_331_out, not_332_out, not_333_out, not_334_out, not_335_out, not_336_out,
       not_337_out, not_338_out, not_339_out, not_340_out, not_341_out, not_342_out, not_343_out,
       not_344_out, not_345_out, not_346_out, not_347_out, not_348_out, not_349_out, not_350_out,
       not_351_out, not_352_out, not_353_out, not_354_out, not_355_out, not_356_out, not_357_out,
       not_358_out, not_359_out, not_360_out, not_361_out, not_362_out, not_363_out, not_364_out,
       not_365_out, not_366_out, not_367_out, not_368_out, not_369_out, not_370_out, not_371_out,
       not_372_out, not_373_out, not_374_out, not_375_out, not_376_out, not_377_out, not_378_out,
       not_379_out, not_380_out, not_381_out, not_382_out, not_383_out;

  not not_1 (not_1_out, in_1);
  not not_2 (not_2_out, not_1_out);
  not not_3 (not_3_out, not_339_out);
  not not_4 (not_4_out, not_3_out);
  not not_5 (not_5_out, not_342_out);
  not not_6 (not_6_out, not_5_out);
  not not_7 (not_7_out, not_345_out);
  not not_8 (not_8_out, not_7_out);
  not not_9 (not_9_out, not_348_out);
  not not_10 (not_10_out, not_9_out);
  not not_11 (not_11_out, not_351_out);
  not not_12 (not_12_out, not_11_out);
  not not_13 (not_13_out, not_354_out);
  not not_14 (not_14_out, not_13_out);
  not not_15 (not_15_out, not_357_out);
  not not_16 (not_16_out, not_15_out);
  not not_17 (not_17_out, not_360_out);
  not not_18 (not_18_out, not_17_out);
  not not_19 (not_19_out, not_363_out);
  not not_20 (not_20_out, not_19_out);
  not not_21 (not_21_out, not_366_out);
  not not_22 (not_22_out, not_21_out);
  not not_23 (not_23_out, not_369_out);
  not not_24 (not_24_out, not_23_out);
  not not_25 (not_25_out, not_372_out);
  not not_26 (not_26_out, not_25_out);
  not not_27 (not_27_out, not_375_out);
  not not_28 (not_28_out, not_27_out);
  not not_29 (not_29_out, not_378_out);
  not not_30 (not_30_out, not_29_out);
  not not_31 (not_31_out, not_381_out);
  not not_32 (not_32_out, not_31_out);
  not not_33 (not_33_out, not_2_out);
  not not_34 (not_34_out, not_33_out);
  not not_35 (not_35_out, not_34_out);
  not not_36 (not_36_out, not_4_out);
  not not_37 (not_37_out, not_36_out);
  not not_38 (not_38_out, not_37_out);
  not not_39 (not_39_out, not_6_out);
  not not_40 (not_40_out, not_39_out);
  not not_41 (not_41_out, not_40_out);
  not not_42 (not_42_out, not_8_out);
  not not_43 (not_43_out, not_42_out);
  not not_44 (not_44_out, not_43_out);
  not not_45 (not_45_out, not_10_out);
  not not_46 (not_46_out, not_45_out);
  not not_47 (not_47_out, not_46_out);
  not not_48 (not_48_out, not_12_out);
  not not_49 (not_49_out, not_48_out);
  not not_50 (not_50_out, not_49_out);
  not not_51 (not_51_out, not_14_out);
  not not_52 (not_52_out, not_51_out);
  not not_53 (not_53_out, not_52_out);
  not not_54 (not_54_out, not_16_out);
  not not_55 (not_55_out, not_54_out);
  not not_56 (not_56_out, not_55_out);
  not not_57 (not_57_out, not_18_out);
  not not_58 (not_58_out, not_57_out);
  not not_59 (not_59_out, not_58_out);
  not not_60 (not_60_out, not_20_out);
  not not_61 (not_61_out, not_60_out);
  not not_62 (not_62_out, not_61_out);
  not not_63 (not_63_out, not_22_out);
  not not_64 (not_64_out, not_63_out);
  not not_65 (not_65_out, not_64_out);
  not not_66 (not_66_out, not_24_out);
  not not_67 (not_67_out, not_66_out);
  not not_68 (not_68_out, not_67_out);
  not not_69 (not_69_out, not_26_out);
  not not_70 (not_70_out, not_69_out);
  not not_71 (not_71_out, not_70_out);
  not not_72 (not_72_out, not_28_out);
  not not_73 (not_73_out, not_72_out);
  not not_74 (not_74_out, not_73_out);
  not not_75 (not_75_out, not_30_out);
  not not_76 (not_76_out, not_75_out);
  not not_77 (not_77_out, not_76_out);
  not not_78 (not_78_out, not_32_out);
  not not_79 (not_79_out, not_78_out);
  not not_80 (not_80_out, not_79_out);
  not not_81 (not_81_out, not_35_out);
  not not_82 (not_82_out, not_81_out);
  not not_83 (not_83_out, not_82_out);
  not not_84 (not_84_out, not_38_out);
  not not_85 (not_85_out, not_84_out);
  not not_86 (not_86_out, not_85_out);
  not not_87 (not_87_out, not_41_out);
  not not_88 (not_88_out, not_87_out);
  not not_89 (not_89_out, not_88_out);
  not not_90 (not_90_out, not_44_out);
  not not_91 (not_91_out, not_90_out);
  not not_92 (not_92_out, not_91_out);
  not not_93 (not_93_out, not_47_out);
  not not_94 (not_94_out, not_93_out);
  not not_95 (not_95_out, not_94_out);
  not not_96 (not_96_out, not_50_out);
  not not_97 (not_97_out, not_96_out);
  not not_98 (not_98_out, not_97_out);
  not not_99 (not_99_out, not_53_out);
  not not_100 (not_100_out, not_99_out);
  not not_101 (not_101_out, not_100_out);
  not not_102 (not_102_out, not_56_out);
  not not_103 (not_103_out, not_102_out);
  not not_104 (not_104_out, not_103_out);
  not not_105 (not_105_out, not_59_out);
  not not_106 (not_106_out, not_105_out);
  not not_107 (not_107_out, not_106_out);
  not not_108 (not_108_out, not_62_out);
  not not_109 (not_109_out, not_108_out);
  not not_110 (not_110_out, not_109_out);
  not not_111 (not_111_out, not_65_out);
  not not_112 (not_112_out, not_111_out);
  not not_113 (not_113_out, not_112_out);
  not not_114 (not_114_out, not_68_out);
  not not_115 (not_115_out, not_114_out);
  not not_116 (not_116_out, not_115_out);
  not not_117 (not_117_out, not_71_out);
  not not_118 (not_118_out, not_117_out);
  not not_119 (not_119_out, not_118_out);
  not not_120 (not_120_out, not_74_out);
  not not_121 (not_121_out, not_120_out);
  not not_122 (not_122_out, not_121_out);
  not not_123 (not_123_out, not_77_out);
  not not_124 (not_124_out, not_123_out);
  not not_125 (not_125_out, not_124_out);
  not not_126 (not_126_out, not_80_out);
  not not_127 (not_127_out, not_126_out);
  not not_128 (not_128_out, not_127_out);
  not not_129 (not_129_out, not_83_out);
  not not_130 (not_130_out, not_129_out);
  not not_131 (not_131_out, not_86_out);
  not not_132 (not_132_out, not_131_out);
  not not_133 (not_133_out, not_89_out);
  not not_134 (not_134_out, not_133_out);
  not not_135 (not_135_out, not_92_out);
  not not_136 (not_136_out, not_135_out);
  not not_137 (not_137_out, not_95_out);
  not not_138 (not_138_out, not_137_out);
  not not_139 (not_139_out, not_98_out);
  not not_140 (not_140_out, not_139_out);
  not not_141 (not_141_out, not_101_out);
  not not_142 (not_142_out, not_141_out);
  not not_143 (not_143_out, not_104_out);
  not not_144 (not_144_out, not_143_out);
  not not_145 (not_145_out, not_107_out);
  not not_146 (not_146_out, not_145_out);
  not not_147 (not_147_out, not_110_out);
  not not_148 (not_148_out, not_147_out);
  not not_149 (not_149_out, not_113_out);
  not not_150 (not_150_out, not_149_out);
  not not_151 (not_151_out, not_116_out);
  not not_152 (not_152_out, not_151_out);
  not not_153 (not_153_out, not_119_out);
  not not_154 (not_154_out, not_153_out);
  not not_155 (not_155_out, not_122_out);
  not not_156 (not_156_out, not_155_out);
  not not_157 (not_157_out, not_125_out);
  not not_158 (not_158_out, not_157_out);
  not not_159 (not_159_out, not_128_out);
  not not_160 (not_160_out, not_159_out);
  not not_161 (not_161_out, not_130_out);
  not not_162 (not_162_out, not_161_out);
  not not_163 (not_163_out, not_162_out);
  not not_164 (not_164_out, not_132_out);
  not not_165 (not_165_out, not_164_out);
  not not_166 (not_166_out, not_165_out);
  not not_167 (not_167_out, not_134_out);
  not not_168 (not_168_out, not_167_out);
  not not_169 (not_169_out, not_168_out);
  not not_170 (not_170_out, not_136_out);
  not not_171 (not_171_out, not_170_out);
  not not_172 (not_172_out, not_171_out);
  not not_173 (not_173_out, not_138_out);
  not not_174 (not_174_out, not_173_out);
  not not_175 (not_175_out, not_174_out);
  not not_176 (not_176_out, not_140_out);
  not not_177 (not_177_out, not_176_out);
  not not_178 (not_178_out, not_177_out);
  not not_179 (not_179_out, not_142_out);
  not not_180 (not_180_out, not_179_out);
  not not_181 (not_181_out, not_180_out);
  not not_182 (not_182_out, not_144_out);
  not not_183 (not_183_out, not_182_out);
  not not_184 (not_184_out, not_183_out);
  not not_185 (not_185_out, not_146_out);
  not not_186 (not_186_out, not_185_out);
  not not_187 (not_187_out, not_186_out);
  not not_188 (not_188_out, not_148_out);
  not not_189 (not_189_out, not_188_out);
  not not_190 (not_190_out, not_189_out);
  not not_191 (not_191_out, not_150_out);
  not not_192 (not_192_out, not_191_out);
  not not_193 (not_193_out, not_192_out);
  not not_194 (not_194_out, not_152_out);
  not not_195 (not_195_out, not_194_out);
  not not_196 (not_196_out, not_195_out);
  not not_197 (not_197_out, not_154_out);
  not not_198 (not_198_out, not_197_out);
  not not_199 (not_199_out, not_198_out);
  not not_200 (not_200_out, not_156_out);
  not not_201 (not_201_out, not_200_out);
  not not_202 (not_202_out, not_201_out);
  not not_203 (not_203_out, not_158_out);
  not not_204 (not_204_out, not_203_out);
  not not_205 (not_205_out, not_204_out);
  not not_206 (not_206_out, not_160_out);
  not not_207 (not_207_out, not_206_out);
  not not_208 (not_208_out, not_207_out);
  not not_209 (not_209_out, not_163_out);
  not not_210 (not_210_out, not_209_out);
  not not_211 (not_211_out, not_210_out);
  not not_212 (not_212_out, not_166_out);
  not not_213 (not_213_out, not_212_out);
  not not_214 (not_214_out, not_213_out);
  not not_215 (not_215_out, not_169_out);
  not not_216 (not_216_out, not_215_out);
  not not_217 (not_217_out, not_216_out);
  not not_218 (not_218_out, not_172_out);
  not not_219 (not_219_out, not_218_out);
  not not_220 (not_220_out, not_219_out);
  not not_221 (not_221_out, not_175_out);
  not not_222 (not_222_out, not_221_out);
  not not_223 (not_223_out, not_222_out);
  not not_224 (not_224_out, not_178_out);
  not not_225 (not_225_out, not_224_out);
  not not_226 (not_226_out, not_225_out);
  not not_227 (not_227_out, not_181_out);
  not not_228 (not_228_out, not_227_out);
  not not_229 (not_229_out, not_228_out);
  not not_230 (not_230_out, not_184_out);
  not not_231 (not_231_out, not_230_out);
  not not_232 (not_232_out, not_231_out);
  not not_233 (not_233_out, not_187_out);
  not not_234 (not_234_out, not_233_out);
  not not_235 (not_235_out, not_234_out);
  not not_236 (not_236_out, not_190_out);
  not not_237 (not_237_out, not_236_out);
  not not_238 (not_238_out, not_237_out);
  not not_239 (not_239_out, not_193_out);
  not not_240 (not_240_out, not_239_out);
  not not_241 (not_241_out, not_240_out);
  not not_242 (not_242_out, not_196_out);
  not not_243 (not_243_out, not_242_out);
  not not_244 (not_244_out, not_243_out);
  not not_245 (not_245_out, not_199_out);
  not not_246 (not_246_out, not_245_out);
  not not_247 (not_247_out, not_246_out);
  not not_248 (not_248_out, not_202_out);
  not not_249 (not_249_out, not_248_out);
  not not_250 (not_250_out, not_249_out);
  not not_251 (not_251_out, not_205_out);
  not not_252 (not_252_out, not_251_out);
  not not_253 (not_253_out, not_252_out);
  not not_254 (not_254_out, not_208_out);
  not not_255 (not_255_out, not_254_out);
  not not_256 (not_256_out, not_255_out);
  not not_257 (not_257_out, not_211_out);
  not not_258 (not_258_out, not_257_out);
  not not_259 (not_259_out, not_214_out);
  not not_260 (not_260_out, not_259_out);
  not not_261 (not_261_out, not_217_out);
  not not_262 (not_262_out, not_261_out);
  not not_263 (not_263_out, not_220_out);
  not not_264 (not_264_out, not_263_out);
  not not_265 (not_265_out, not_223_out);
  not not_266 (not_266_out, not_265_out);
  not not_267 (not_267_out, not_226_out);
  not not_268 (not_268_out, not_267_out);
  not not_269 (not_269_out, not_229_out);
  not not_270 (not_270_out, not_269_out);
  not not_271 (not_271_out, not_232_out);
  not not_272 (not_272_out, not_271_out);
  not not_273 (not_273_out, not_235_out);
  not not_274 (not_274_out, not_273_out);
  not not_275 (not_275_out, not_238_out);
  not not_276 (not_276_out, not_275_out);
  not not_277 (not_277_out, not_241_out);
  not not_278 (not_278_out, not_277_out);
  not not_279 (not_279_out, not_244_out);
  not not_280 (not_280_out, not_279_out);
  not not_281 (not_281_out, not_247_out);
  not not_282 (not_282_out, not_281_out);
  not not_283 (not_283_out, not_250_out);
  not not_284 (not_284_out, not_283_out);
  not not_285 (not_285_out, not_253_out);
  not not_286 (not_286_out, not_285_out);
  not not_287 (not_287_out, not_256_out);
  not not_288 (not_288_out, not_287_out);
  not not_289 (not_289_out, not_258_out);
  not not_290 (not_290_out, not_289_out);
  not not_291 (not_291_out, not_290_out);
  not not_292 (not_292_out, not_260_out);
  not not_293 (not_293_out, not_292_out);
  not not_294 (not_294_out, not_293_out);
  not not_295 (not_295_out, not_262_out);
  not not_296 (not_296_out, not_295_out);
  not not_297 (not_297_out, not_296_out);
  not not_298 (not_298_out, not_264_out);
  not not_299 (not_299_out, not_298_out);
  not not_300 (not_300_out, not_299_out);
  not not_301 (not_301_out, not_266_out);
  not not_302 (not_302_out, not_301_out);
  not not_303 (not_303_out, not_302_out);
  not not_304 (not_304_out, not_268_out);
  not not_305 (not_305_out, not_304_out);
  not not_306 (not_306_out, not_305_out);
  not not_307 (not_307_out, not_270_out);
  not not_308 (not_308_out, not_307_out);
  not not_309 (not_309_out, not_308_out);
  not not_310 (not_310_out, not_272_out);
  not not_311 (not_311_out, not_310_out);
  not not_312 (not_312_out, not_311_out);
  not not_313 (not_313_out, not_274_out);
  not not_314 (not_314_out, not_313_out);
  not not_315 (not_315_out, not_314_out);
  not not_316 (not_316_out, not_276_out);
  not not_317 (not_317_out, not_316_out);
  not not_318 (not_318_out, not_317_out);
  not not_319 (not_319_out, not_278_out);
  not not_320 (not_320_out, not_319_out);
  not not_321 (not_321_out, not_320_out);
  not not_322 (not_322_out, not_280_out);
  not not_323 (not_323_out, not_322_out);
  not not_324 (not_324_out, not_323_out);
  not not_325 (not_325_out, not_282_out);
  not not_326 (not_326_out, not_325_out);
  not not_327 (not_327_out, not_326_out);
  not not_328 (not_328_out, not_284_out);
  not not_329 (not_329_out, not_328_out);
  not not_330 (not_330_out, not_329_out);
  not not_331 (not_331_out, not_286_out);
  not not_332 (not_332_out, not_331_out);
  not not_333 (not_333_out, not_332_out);
  not not_334 (not_334_out, not_288_out);
  not not_335 (not_335_out, not_334_out);
  not not_336 (not_336_out, not_335_out);
  not not_337 (not_337_out, not_291_out);
  not not_338 (not_338_out, not_337_out);
  not not_339 (not_339_out, not_338_out);
  not not_340 (not_340_out, not_294_out);
  not not_341 (not_341_out, not_340_out);
  not not_342 (not_342_out, not_341_out);
  not not_343 (not_343_out, not_297_out);
  not not_344 (not_344_out, not_343_out);
  not not_345 (not_345_out, not_344_out);
  not not_346 (not_346_out, not_300_out);
  not not_347 (not_347_out, not_346_out);
  not not_348 (not_348_out, not_347_out);
  not not_349 (not_349_out, not_303_out);
  not not_350 (not_350_out, not_349_out);
  not not_351 (not_351_out, not_350_out);
  not not_352 (not_352_out, not_306_out);
  not not_353 (not_353_out, not_352_out);
  not not_354 (not_354_out, not_353_out);
  not not_355 (not_355_out, not_309_out);
  not not_356 (not_356_out, not_355_out);
  not not_357 (not_357_out, not_356_out);
  not not_358 (not_358_out, not_312_out);
  not not_359 (not_359_out, not_358_out);
  not not_360 (not_360_out, not_359_out);
  not not_361 (not_361_out, not_315_out);
  not not_362 (not_362_out, not_361_out);
  not not_363 (not_363_out, not_362_out);
  not not_364 (not_364_out, not_318_out);
  not not_365 (not_365_out, not_364_out);
  not not_366 (not_366_out, not_365_out);
  not not_367 (not_367_out, not_321_out);
  not not_368 (not_368_out, not_367_out);
  not not_369 (not_369_out, not_368_out);
  not not_370 (not_370_out, not_324_out);
  not not_371 (not_371_out, not_370_out);
  not not_372 (not_372_out, not_371_out);
  not not_373 (not_373_out, not_327_out);
  not not_374 (not_374_out, not_373_out);
  not not_375 (not_375_out, not_374_out);
  not not_376 (not_376_out, not_330_out);
  not not_377 (not_377_out, not_376_out);
  not not_378 (not_378_out, not_377_out);
  not not_379 (not_379_out, not_333_out);
  not not_380 (not_380_out, not_379_out);
  not not_381 (not_381_out, not_380_out);
  not not_382 (not_382_out, not_336_out);
  not not_383 (not_383_out, not_382_out);
  not not_384 (out_2, not_383_out);
endmodule

module next_index (
  input  [1:0] cmd,
  input  sync,
  input  [2:0] index,
  output [2:0] next_idx
);

  wire xor_1_out;
  wire [2:0] and_1_out, bits_mod_5_1_out_2, bits_mod_5_2_out_2;
  wire [3:0] and_3_out, bit_extender_1_out;

  xor xor_1 (xor_1_out, cmd[0], cmd[1]);
  assign bit_extender_1_out = {{3{sync}}, sync};  // Bit_Extender bit_extender_1
  and and_1 (and_1_out[0], cmd[0], xor_1_out);
  and and_2 (and_1_out[2], xor_1_out, cmd[1]);
  bits_mod_5 bits_mod_5_1 (.in_1({1'b0, index}), .out_2(bits_mod_5_1_out_2));
  assign and_3_out = {1'b0, and_1_out[2], 1'b0, and_1_out[0]} & bit_extender_1_out;  // AND_Gate and_3, 4 bits wide
  plus_3_bits_mod_5 plus_3_bits_mod_5_1 (.in_1(bits_mod_5_2_out_2), .in_2(bits_mod_5_1_out_2), .out_3(next_idx));
  bits_mod_5 bits_mod_5_2 (.in_1(and_3_out), .out_2(bits_mod_5_2_out_2));
endmodule

module bits_mod_5 (
  input  [3:0] in_1,
  output [2:0] out_2
);

  wire and_1_out, and_2_out, and_3_out, and_4_out, and_5_out, and_6_out, and_7_out, and_8_out,
       dec_3_8_1_out_4, dec_3_8_1_out_5, dec_3_8_1_out_6, dec_3_8_1_out_7, dec_3_8_1_out_8, dec_3_8_1_out_9,
       dec_3_8_1_out_10, dec_3_8_1_out_11, dec_3_8_2_out_4, dec_3_8_2_out_5, dec_3_8_2_out_6,
       dec_3_8_2_out_7, dec_3_8_2_out_8, dec_3_8_2_out_9, dec_3_8_2_out_10, dec_3_8_2_out_11, or_1_out,
       or_2_out, or_3_out, or_4_out, or_5_out;

  and and_1 (and_1_out, in_1[0], ~in_1[3]);  // AND_Gate
  and and_2 (and_2_out, in_1[1], ~in_1[3]);  // AND_Gate
  and and_3 (and_3_out, in_1[2], ~in_1[3]);  // AND_Gate
  and and_4 (and_4_out, in_1[0], in_1[3]);
  and and_5 (and_5_out, in_1[1], in_1[3]);
  and and_6 (and_6_out, in_1[2], in_1[3]);
  dec_3_8 dec_3_8_1 (
    .in_1(and_1_out), .in_2(and_2_out), .in_3(and_3_out), .out_4(dec_3_8_1_out_4), .out_5(dec_3_8_1_out_5),
    .out_6(dec_3_8_1_out_6), .out_7(dec_3_8_1_out_7), .out_8(dec_3_8_1_out_8), .out_9(dec_3_8_1_out_9),
    .out_10(dec_3_8_1_out_10), .out_11(dec_3_8_1_out_11));
  dec_3_8 dec_3_8_2 (
    .in_1(and_4_out), .in_2(and_5_out), .in_3(and_6_out), .out_4(dec_3_8_2_out_4), .out_5(dec_3_8_2_out_5),
    .out_6(dec_3_8_2_out_6), .out_7(dec_3_8_2_out_7), .out_8(dec_3_8_2_out_8), .out_9(dec_3_8_2_out_9),
    .out_10(dec_3_8_2_out_10), .out_11(dec_3_8_2_out_11));
  and and_7 (and_7_out, ~in_1[3], dec_3_8_1_out_4);  // AND_Gate
  and and_8 (and_8_out, in_1[3], dec_3_8_2_out_4);
  or or_1 (or_1_out, and_7_out, dec_3_8_1_out_9, dec_3_8_2_out_6, dec_3_8_2_out_11);
  or or_2 (or_2_out, dec_3_8_1_out_5, dec_3_8_1_out_10, dec_3_8_2_out_7);
  or or_3 (or_3_out, dec_3_8_1_out_6, dec_3_8_1_out_11, dec_3_8_2_out_8);
  or or_4 (or_4_out, dec_3_8_1_out_7, and_8_out, dec_3_8_2_out_9);
  or or_5 (or_5_out, dec_3_8_1_out_8, dec_3_8_2_out_5, dec_3_8_2_out_10);
  code_5_to_3 code_5_to_3_1 (
    .in_1(or_1_out), .in_2(or_2_out), .in_3(or_3_out), .in_4(or_4_out), .in_5(or_5_out), .out_6(out_2));
endmodule

module convert_to_neg_val (
  input  [4:0] in_1,
  output [4:0] out_2
);

  wire [4:0] not_1_out;

  assign not_1_out = ~in_1;  // NOT_Gate not_1, 5 bits wide
  plus_5_bits plus_5_bits_1 (.in_1(not_1_out), .in_2(5'b00001), .q(out_2));  // open: c
endmodule

module plus_4_bits (
  input  [3:0] in_1,
  input  [3:0] in_2,
  output [3:0] q,
  output c
);

  wire plus_3_bits_1_c;

  plus_3_bits plus_3_bits_1 (.in_1(in_1[2:0]), .in_2(in_2[2:0]), .q(q[2:0]), .c(plus_3_bits_1_c));
  plus3 plus3_1 (.in_1(plus_3_bits_1_c), .in_2(in_1[3]), .in_3(in_2[3]), .s(q[3]), .c(c));
endmodule

module plus_5_bits (
  input  [4:0] in_1,
  input  [4:0] in_2,
  output [4:0] q,
  output c
);

  wire plus_4_bits_1_c;

  plus_4_bits plus_4_bits_1 (.in_1(in_1[3:0]), .in_2(in_2[3:0]), .q(q[3:0]), .c(plus_4_bits_1_c));
  plus3 plus3_1 (.in_1(plus_4_bits_1_c), .in_2(in_1[4]), .in_3(in_2[4]), .s(q[4]), .c(c));
endmodule

module dec_3_8 (
  input  in_1,
  input  in_2,
  input  in_3,
  output out_4,
  output out_5,
  output out_6,
  output out_7,
  output out_8,
  output out_9,
  output out_10,
  output out_11
);

  and and_1 (out_4, ~in_1, ~in_2, ~in_3);  // AND_Gate
  and and_2 (out_5, in_1, ~in_2, ~in_3);  // AND_Gate
  and and_3 (out_6, ~in_1, in_2, ~in_3);  // AND_Gate
  and and_4 (out_7, in_1, in_2, ~in_3);  // AND_Gate
  and and_5 (out_8, ~in_1, ~in_2, in_3);  // AND_Gate
  and and_6 (out_9, in_1, ~in_2, in_3);  // AND_Gate
  and and_7 (out_10, ~in_1, in_2, in_3);  // AND_Gate
  and and_8 (out_11, in_1, in_2, in_3);
endmodule

module code_5_to_3 (
  input  in_1,
  input  in_2,
  input  in_3,
  input  in_4,
  input  in_5,
  output [2:0] out_6
);

  wire [2:0] and_1_out, and_2_out, and_3_out, and_4_out, and_5_out;

  assign and_1_out = 3'b000 & {3{in_1}};  // AND_Gate and_1, 3 bits wide
  assign and_2_out = 3'b001 & {3{in_2}};  // AND_Gate and_2, 3 bits wide
  assign and_3_out = 3'b010 & {3{in_3}};  // AND_Gate and_3, 3 bits wide
  assign and_4_out = 3'b011 & {3{in_4}};  // AND_Gate and_4, 3 bits wide
  assign and_5_out = 3'b100 & {3{in_5}};  // AND_Gate and_5, 3 bits wide
  assign out_6 = and_1_out | and_2_out | and_3_out | and_4_out | and_5_out;  // OR_Gate or_1, 3 bits wide
endmodule

module inout_cmd (
  input  [1:0] cmd,
  input  [3:0] program_out,
  output [3:0] inpout
);

  wire not_1_out;

  Transistor #(.\type ("n"), .width(4)) transistor_1 (.in(program_out), .out(inpout), .gate(cmd[1]));
  not not_1 (not_1_out, cmd[1]);
  Transistor #(.width(4)) transistor_2 (.in(program_out), .out(inpout), .gate(not_1_out));
endmodule

module stack_copy (
  input  reset,
  input  [1:0] cmd,
  input  sync,
  input  [2:0] index,
  input  [3:0] IO_DATA_in,
  output [3:0] out_6,
  output [3:0] out_7,
  output [3:0] out_8,
  output [3:0] out_9,
  output [3:0] out_10,
  output [3:0] IO_DATA_out
);

  wire not_1_out;
  wire [1:0] CMD_t;
  wire [2:0] current_index_1_index, d_3_bits_trigger_1_q, shift_index_1_out_5;
  wire [3:0] DATA, memory_1_q;

  d_2_bits_trigger d_2_bits_trigger_1 (.reset(reset), .sync(sync), .d(cmd), .q(CMD_t));
  current_index current_index_1 (.reset(reset), .cmd(CMD_t), .sync(sync), .index(current_index_1_index));
  not not_1 (not_1_out, sync);
  inout_cmd inout_cmd_1 (.cmd(CMD_t), .program_out(memory_1_q), .inpout(IO_DATA_in));
  shift_index shift_index_1 (
    .cmd(CMD_t), .sync(sync), .curr_idx(current_index_1_index), .index(index), .out_5(shift_index_1_out_5));
  d_3_bits_trigger d_3_bits_trigger_1 (.reset(reset), .sync(sync), .d(shift_index_1_out_5), .q(d_3_bits_trigger_1_q));
  d_4_bits_trigger d_4_bits_trigger_1 (.reset(reset), .sync(sync), .d(IO_DATA_in), .q(DATA));
  memory memory_1 (
    .reset(reset), .sync(not_1_out), .cmd(CMD_t), .index(d_3_bits_trigger_1_q), .data(DATA), .q0(out_10),
    .q1(out_6), .q2(out_7), .q3(out_8), .q4(out_9), .Q(memory_1_q));

  assign IO_DATA_out = IO_DATA_in;

  // Other names for the same wires on the sheet: D0[3:0] = out_6; D1[3:0] = out_7; D2[3:0] = out_8; D3[3:0] = out_9;
  //   D4[3:0] = out_10
endmodule

module d_2_bits_trigger (
  input  reset,
  input  sync,
  input  [1:0] d,
  output [1:0] q
);

  wire d0, d1, d_trigger_1_neg_q, d_trigger_2_neg_q, not_1_out, SYNC_t;
  wire [1:0] bit_extender_1_out;

  not not_1 (not_1_out, reset);
  assign bit_extender_1_out = {{1{not_1_out}}, not_1_out};  // Bit_Extender bit_extender_1
  assign {d1, d0} = bit_extender_1_out & d;  // AND_Gate and_1, 2 bits wide
  or or_1 (SYNC_t, reset, sync);
  d_trigger d_trigger_1 (.d(d0), .c(SYNC_t), .q(q[0]), .neg_q(d_trigger_1_neg_q));
  d_trigger d_trigger_2 (.d(d1), .c(SYNC_t), .q(q[1]), .neg_q(d_trigger_2_neg_q));
endmodule
