// Logisim project stack_logical_lite.circ as structural Verilog: 2 circuits, main circuit main
module main (
  input  CLK,
  input  RESET,
  input  [1:0] COMMAND,
  input  [2:0] INDEX,
  input  [3:0] IDATA,
  output [3:0] ODATA
);

  wire [3:0] stack_1_d0, stack_1_d1, stack_1_d2, stack_1_d3, stack_1_d4, stack_1_d5, stack_1_d6, stack_1_d7;

  // Probe on stack_1_d0
  stack stack_1 (
    .CLK(CLK), .RESET(RESET), .COMMAND(COMMAND), .INDEX(INDEX), .IDATA(IDATA), .d0(stack_1_d0),
    .d1(stack_1_d1), .d2(stack_1_d2), .d3(stack_1_d3), .d4(stack_1_d4), .d5(stack_1_d5), .d6(stack_1_d6),
    .d7(stack_1_d7), .ODATA(ODATA));
  // Probe on stack_1_d1
  // Probe on stack_1_d2
  // Probe on stack_1_d3
  // Probe on stack_1_d4
  // Probe on stack_1_d5
  // Probe on stack_1_d6
  // Probe on stack_1_d7
endmodule

module stack (
  input  CLK,
  input  RESET,
  input  [1:0] COMMAND,
  input  [2:0] INDEX,
  input  [3:0] IDATA,
  output [3:0] d0,
  output [3:0] d1,
  output [3:0] d2,
  output [3:0] d3,
  output [3:0] d4,
  output [3:0] d5,
  output [3:0] d6,
  output [3:0] d7,
  output [3:0] ODATA
);


  // Notes on the sheet:
  //   your circuit must be here
endmodule
